# Fritzing sketch N64 (saved by Fritzing 0.7.11b)
breadboards: 1

parts:
  Arduino2 = Arduino
  J2 = Piezo Speaker
  LED1 = LED - 5mm [color="Red (633nm)" package="5 mm [THT]"]
  R1 = Resistor [tolerance=±5% resistance=220 package="0805 [SMD]"]
  U1 = mystery part, 3 pins [chip_label="N64 Controller"]

nets:
  N1: Arduino2.GND, J2.pin1, R1.Pin_1, U1.pin1
  N2: Arduino2.D13, J2.pin2
  N3: Arduino2.D9, LED1.anode
  N4: Arduino2.D2, U1.pin2
  N5: Arduino2.3V3, U1.pin3
  N6: LED1.cathode, R1.Pin_0
